# Fritzing sketch trackerAPRS (saved by Fritzing 0.9.3b)
circuit board: 8.46667cm x 5.64444cm
perfboards: 1

parts:
  DRA_In = Header 8 [package=1x08_smd]
  Composant1 = Arduino Nano (Rev3.0)
  ANT_VHF = U.FL [package=u.fl]
  Audio_Jack = 3.5mm Audio Jack [package=audio-jack-3.5mm-smd]
  DRA = Header 8 [package=1x08_smd]
  R1 = Resistor [tolerance=±5% resistance=2.2k package="0805 [SMD]"]
  R2 = Resistor [tolerance=±5% resistance=2.2k package="0805 [SMD]"]
  R3 = Resistor [tolerance=±5% resistance=1k package="0805 [SMD]"]
  R4 = Resistor [tolerance=±5% resistance=2.2k package="0805 [SMD]"]
  R5 = Resistor [tolerance=±5% resistance=1k package="0805 [SMD]"]
  R6 = Resistor [tolerance=±5% resistance=1k package="0805 [SMD]"]
  Diode_5V-0_6V = Diode [package=diode-hv]
  R7 = Resistor [tolerance=±5% resistance=2.2k package="0805 [SMD]"]
  R8 = Resistor [tolerance=±5% resistance=4.7k package="0805 [SMD]"]
  R9 = Resistor [tolerance=±5% resistance=1k package="0805 [SMD]"]
  2N2222 = TRANSISTOR_NPN [package=to-92]
  R10 = Resistor [tolerance=±5% resistance=1k package="0805 [SMD]"]
  R11 = Resistor [tolerance=±5% resistance=2.2k package="0805 [SMD]"]
  R12 = Resistor [tolerance=±5% resistance=1k package="0805 [SMD]"]
  R13 = Resistor [tolerance=±5% resistance=1k package="0805 [SMD]"]
  R14 = Resistor [tolerance=±5% resistance=1k package="0805 [SMD]"]
  R15 = Resistor [tolerance=±5% resistance=100k package="0805 [SMD]"]
  R16 = Resistor [tolerance=±5% resistance=2.2k package="0805 [SMD]"]
  R17 = Resistor [tolerance=±5% resistance=2.2k package="0805 [SMD]"]
  R18 = Resistor [tolerance=±5% resistance=2.2k package="0805 [SMD]"]
  DRA818V = SA818 DRA818 VHF UHF transmitter
  Low_Power = Jumper [package=sj_2s-no]
  U4 = NEO 6M GPS
  C1 = Ceramic Capacitor [capacitance=100nF package="100 mil [THT, multilayer]"]
  IO = Header 8 [package=1x08_smd]
  Button = Pushbutton [package="[THT]"]

nets:
  N1: DRA_In.1, DRA818V.pin_6
  N2: DRA_In.3, DRA818V.pin_18_MIC_IN
  N3: DRA_In.4, DRA818V.pin_16
  N4: DRA_In.5, DRA818V.pin_17
  N5: DRA_In.6, DRA818V.pin_5
  N6: DRA_In.7, ANT_VHF.GND, DRA818V.pin_9, Low_Power.2
  N7: DRA_In.8, DRA818V.pin_8
  N8: Composant1.D1/TX, IO.4
  GND: Composant1.GND, R11.Pin_1, R16.Pin_0, R17.Pin_1, R18.Pin_0, U4.GND, Button.Pin_2
  N9: Composant1.D2, R3.Pin_0
  N10: Composant1.D3, DRA.5
  N11: Composant1.D4, R6.Pin_0
  N12: Composant1.D5, R5.Pin_0
  N13: Composant1.D6, U4.TXD
  N14: Composant1.D7, Button.Pin_3, Button.Pin_4
  N15: Composant1.D8, R7.Pin_0
  N16: Composant1.D9, R4.Pin_0
  N17: Composant1.D10, R2.Pin_0
  N18: Composant1.D11/MOSI, R1.Pin_0
  N19: Composant1.D12/MISO, R8.Pin_0
  N20: Composant1.VIN, Diode_5V-0_6V.A, IO.6, IO.7
  5V: Composant1.5V
  3V3: Composant1.3V3, U4.VCC
  N21: ANT_VHF.SIGNAL, DRA818V.pin_12
  N22: Audio_Jack.RIGHT, DRA.3, C1.0, IO.2
  N23: Audio_Jack.SLEEVE, R15.Pin_1
  N24: DRA.1, R5.Pin_1, R16.Pin_1
  N25: DRA.4, R6.Pin_1, R17.Pin_0
  N26: DRA.6, R3.Pin_1, R18.Pin_1
  N27: DRA.7, 2N2222.C, IO.3, IO.5
  N28: DRA.8, Diode_5V-0_6V.C
  N29: R1.Pin_1, R12.Pin_1, R13.Pin_1
  N30: R2.Pin_1, R13.Pin_0, R14.Pin_1
  N31: R4.Pin_1, R10.Pin_0, R14.Pin_0
  N32: R7.Pin_1, R10.Pin_1, R11.Pin_0
  N33: R8.Pin_1, 2N2222.B
  N34: R9.Pin_0, IO.1
  N35: R9.Pin_1, 2N2222.E
  N36: R15.Pin_0, C1.1
  N37: DRA818V.pin_7, Low_Power.1

notes:
  Header DRA818
  1 : Enable
  2 : NC
  3 : Audio from Arduino
  4 : RX to DRA
  5 : TX from DRA
  6 : PTT
  7 : GND
  8 : VCC
  Header Baofeng & debug
  1 : PTT
  2 : Audio
  3 : GND
  4 : TX from Arduino
  5 : GND
  6 & 7 : VCC
  PIN Name Function Description
  1 SQ Output Squelch detection.. Low Audio amplifier on
  2 NC Output No connection
  3 AF_OUT Output Audio output pin.
  4 NC --- No connection
  5 PTT Input Tx/Rx control pin: LowTX; High RX
  6 PD Input Power saving control pin: Lowsleep mode; Highnormal mode
  7 H/L Input RF Power Selection: Low0.5W; floated1W
  8 VBAT Power Power supply
  9 GND Ground Ground (0V)
  10 GND Ground Ground (0V)
  11 NC --- No connection
  12 ANT --- Antenna port. 50 Ohm impedance
  13 NC --- No connection
  14 NC --- No connection
  15 NC --- No connection
  16 RXD Input UART input, TTL level
  17 TXD Output UART output, TTL level
  18 MIC_IN Input MIC input
  2-2R resistor network

custom parts:
  SA818 DRA818 VHF UHF transmitter: SA818 high-integrated Embedded walkie talkie module SA818 is a low cost and high performance integrated walkie talkie module. This module is the 2nd generation of the walkie talkie module and the upgraded version of SA808.SA818 comes with built-in high performance microcontroller, narrow band rf transceiver and standard UART interface. It is easy to use. Users only need to add external audio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
  NEO 6M GPS: uSD module
